# Fritzing sketch Project_breadboard (saved by Fritzing 0.9.5d)
breadboards: 1

parts:
  A1 = Esp32-c3 super mini
  R1 = Resistor [tolerance=±5% resistance=220 package="0805 [SMD]"]
  R2 = Resistor [tolerance=±5% resistance=220 package="0805 [SMD]"]
  RGB_Strip_LED3 = RGB Strip LED
  S1 = Pushbutton [package="[SMD]"]
  R3 = Resistor [tolerance=±5% resistance=220 package="0805 [SMD]"]
  LED1 = smd LED [color="Red (633nm)" package="0805 [SMD]"]

nets:
  N1: A1.Pin_4, R1.Pin_0
  N2: A1.Pin_6, S1.Pin_3, S1.Pin_4, R3.Pin_0
  N3: A1.Pin_11, RGB_Strip_LED3.Blue_Connect
  N4: A1.Pin_12, R2.Pin_0
  N5: A1.Pin_13, RGB_Strip_LED3.Green_Connect
  N6: A1.Pin_15, R3.Pin_1
  N7: A1.Pin_16, RGB_Strip_LED3.Common_Connect, S1.Pin_1, S1.Pin_2
  N8: R1.Pin_1, LED1.anode
  N9: R2.Pin_1, RGB_Strip_LED3.Red_Connect

custom parts:
  Esp32-c3 super mini: ESP32-C3 Development Board ESP32 SuperMini Development Board ESP32 Development Board WiFi Bluetooth.
  RGB Strip LED: A tri-color Strip LED with red, green and blue. Based on LED SMD 5050 RGB Pin order: common cathode - green - red - blue
